# Fritzing sketch Fritzing-BinaryClock (saved by Fritzing 0.8.5b)
breadboards: 1

parts:
  U1 = atmega168 [package=dip]
  U3 = 74HC595 [part_number=Columns package="DIP16 [THT]"]
  U2 = 74HC595 [part_number=Rows package="DIP16 [THT]"]
  IC1 = ULN2803A [package=THT]
  8x8_LED_Matrix1 = Led Matrix LD1088-BS
  R1 = Resistor [tolerance=±5% resistance=260 package=THT]
  R2 = Resistor [tolerance=±5% resistance=260 package=THT]
  R3 = Resistor [tolerance=±5% resistance=260 package=THT]
  R4 = Resistor [tolerance=±5% resistance=260 package=THT]
  R5 = Resistor [tolerance=±5% resistance=260 package=THT]
  R6 = Resistor [tolerance=±5% resistance=260 package=THT]
  R7 = Resistor [tolerance=±5% resistance=260 package=THT]
  R8 = Resistor [tolerance=±5% resistance=260 package=THT]
  V1 = DC Power [voltage=5]
  C1 = Capacitor [part_number=100n package=cap-pth-small2]
  R9 = Resistor [tolerance=±5% resistance=10k package=THT]
  C2 = Capacitor [part_number=100n package=cap-pth-small2]
  FTDI_header = FTDI_BASIC [package=ftdi_basic]

nets:
  N1: U1.RESET, R9.Pin_0, C2.1
  N2: U1.D0_(RX), FTDI_header.4
  N3: U1.D1_(TX), FTDI_header.5
  VCC: U1.VCC, U1.AVCC, U3.MR, U3.VCC, U2.MR, U2.VCC, V1.V+, C1.2, R9.Pin_1, FTDI_header.3
  GND: U1.GND, U3.GND, U3.OE, U2.GND, U2.OE, IC1.0V, V1.V-, C1.1, FTDI_header.1
  N4: U1.D8, U3.ST_CP, U2.ST_CP
  N5: U1.D11_(PWM), U3.DS
  N6: U1.D12, U3.SH_CP, U2.SH_CP
  N7: U3.Q1, IC1.In_2
  N8: U3.Q2, IC1.In_3
  N9: U3.Q3, IC1.In_4
  N10: U3.Q4, IC1.In_5
  N11: U3.Q5, IC1.In_6
  N12: U3.Q6, IC1.In_7
  N13: U3.Q7, IC1.In_8
  N14: U3.Q7', U2.DS
  N15: U3.Q0, IC1.In_1
  N16: U2.Q1, R2.Pin_1
  N17: U2.Q2, R3.Pin_1
  N18: U2.Q3, R4.Pin_1
  N19: U2.Q4, R5.Pin_1
  N20: U2.Q5, R6.Pin_1
  N21: U2.Q6, R7.Pin_1
  N22: U2.Q7, R8.Pin_1
  N23: U2.Q0, R1.Pin_1
  N24: IC1.Out_8, 8x8_LED_Matrix1.Pin_16
  N25: IC1.Out_7, 8x8_LED_Matrix1.Pin_15
  N26: IC1.Out_6, 8x8_LED_Matrix1.Pin_11
  N27: IC1.Out_5, 8x8_LED_Matrix1.Pin_6
  N28: IC1.Out_4, 8x8_LED_Matrix1.Pin_10
  N29: IC1.Out_3, 8x8_LED_Matrix1.Pin_4
  N30: IC1.Out_2, 8x8_LED_Matrix1.Pin_3
  N31: IC1.Out_1, 8x8_LED_Matrix1.Pin_13
  N32: 8x8_LED_Matrix1.Pin_1, R5.Pin_0
  N33: 8x8_LED_Matrix1.Pin_2, R7.Pin_0
  N34: 8x8_LED_Matrix1.Pin_5, R8.Pin_0
  N35: 8x8_LED_Matrix1.Pin_7, R6.Pin_0
  N36: 8x8_LED_Matrix1.Pin_8, R3.Pin_0
  N37: 8x8_LED_Matrix1.Pin_9, R1.Pin_0
  N38: 8x8_LED_Matrix1.Pin_12, R4.Pin_0
  N39: 8x8_LED_Matrix1.Pin14, R2.Pin_0
  N40: C2.2, FTDI_header.6

custom parts:
  Led Matrix LD1088-BS: Red Color Common cathode 8x8 LED Matrix
  FTDI_BASIC: FTDI Basic header with labels
